// Logisim project Single_cycle_block.circ as structural Verilog: 1 circuit, main circuit main
module main (
  output [31:0] out_1,
  output [31:0] out_2,
  output [31:0] out_3,
  output [31:0] out_4,
  output [31:0] out_5,
  output [31:0] out_6,
  output [31:0] out_7,
  output [31:0] out_8,
  output [31:0] out_9,
  output [31:0] out_10,
  output [31:0] out_11,
  output [31:0] out_12,
  output [31:0] out_13,
  output [31:0] out_14,
  output [31:0] out_15,
  output [31:0] out_16,
  output [31:0] out_17,
  output [31:0] out_18,
  output [31:0] out_19,
  output [31:0] out_20,
  output [31:0] out_21,
  output [31:0] out_22,
  output [31:0] out_23,
  output [31:0] out_24,
  output [31:0] out_25,
  output [31:0] out_26,
  output [31:0] out_27,
  output [31:0] out_28,
  output [31:0] out_29,
  output [31:0] out_30,
  output [31:0] out_31,
  output [31:0] out_32
);

  wire clock_1_out, EXT_OP, less_falg, less_Unsign_falg, MEM_Read, MEM_Read_EX, MEM_Read_mem, MEM_Write,
       MEM_Write_EX, MEM_Write_mem, Reg_write, Reg_write_EX, reg_write_mem, reg_write_WB, SSET, Stall, WB,
       WB_EX, WB_mem, WB_WB, Zero_flag;
  wire [1:0] ALU_SRC, ALU_SRC_EX, Forwad_B, Forward_A, PC_SELC, Rd_SRC, Rd_SRC_EX, rd_src_mem, rd_src_WB;
  wire [3:0] func_4bit;
  wire [4:0] immd_L, RD_EX, rd_mem, rd_WB, Rs_EX, Rs_ID, Rt_EX, Rt_ID;
  wire [5:0] opcode;
  wire [9:0] ALU_OP, ALU_OP_EX;
  wire [15:0] imm16, imm16_16bit_EX;
  wire [19:0] pc, PC_ID, PC_Plus_1, PC_Plus_1_EX, PC_Plus_1_ID, pc_plus_1_mem, PC_plus_1_WB;
  wire [31:0] alu_1_alu_result, Alu_res_mem, bit_extender_2_out, bit_extender_3_out, bit_extender_4_out,
       Bus_B_mem, BusA_ID, BUSB_EX, immdL_immdU, immdL_immdU_EX, main_3_instruction, main_6_bus_b,
       main_7_out_20, main_9_data_out, main_10_out_10, main_10_out_16, multiplexer_2_out, multiplexer_3_out,
       multiplexer_4_out, multiplexer_5_out;
  wire [31:16] imm16_32_EX;

  Clock clock_1 (.out(clock_1_out));
  // Probe on out_1
  // Probe on out_15
  // Probe on out_29
  // Probe on out_2
  // Probe on out_16
  // Probe on out_30
  // Probe on out_3
  // Probe on out_17
  // Probe on out_31
  // Probe on out_4
  // Probe on out_18
  // Probe on out_32
  pc_new_main main_1 (
    .Pc_Selctor(PC_SELC), .Imm16({imm16[15:9], func_4bit, imm16[4:0]}), .RS1(BusA_ID),
    .Immu({imm16[15:9], func_4bit}), .ImmL(immd_L), .PC_Output(pc), .Clk(clock_1_out), .out_8(PC_Plus_1));
  // Probe on out_5
  // Probe on out_19
  // Probe on out_6
  // Probe on out_7
  // Probe on out_20
  // Probe on out_21
  // Probe on out_8
  // Probe on out_22
  assign immdL_immdU = {{16{imm16[15]}}, {imm16[15:9], func_4bit, immd_L}};  // Bit_Extender bit_extender_1
  // Probe on out_9
  // Probe on out_23
  PC_Control_Unit_main main_2 (
    .in_1(Zero_flag), .in_2(less_falg), .in_3(less_Unsign_falg), .op_code_5bit(opcode[4:0]), .out_5(PC_SELC));
  // Probe on out_10
  // Probe on out_24
  // Probe on out_11
  // Probe on out_25
  // Probe on out_12
  // Probe on out_26
  // Probe on out_13
  // Probe on out_27
  // Probe on out_14
  // Probe on out_28
  main_control_unit main_control_unit_1 (
    .opcode(opcode), .reg_write(Reg_write), .ext_op(EXT_OP), .Rd_src(Rd_SRC), .alu_src(ALU_SRC),
    .mem_write(MEM_Read), .mem_read(MEM_Write), .wb(WB), .Stall(Stall), .out_10(SSET));
  Instruction_Mem_main main_3 (.Address(pc), .Instruction(main_3_instruction));
  // Probe on Rd_SRC
  if_id_main main_4 (
    .Instruction(main_3_instruction), .PC_plus_1(PC_Plus_1),
    .out_6({imm16[15:9], func_4bit, imm16[4:0], Rs_ID, immd_L, opcode}), .out_7(PC_Plus_1_ID),
    .in_5(clock_1_out), .stall(Stall), .PC(pc), .out_8(PC_ID));
  assign bit_extender_2_out = {{16{imm16[15]}}, {imm16[15:9], func_4bit, imm16[4:0]}};  // Bit_Extender bit_extender_2
  assign bit_extender_3_out = {{16{1'b0}}, {imm16[15:9], func_4bit, imm16[4:0]}};  // Bit_Extender bit_extender_3
  Multiplexer #(.width(5), .enable("false")) multiplexer_1 (.in0(imm16[4:0]), .in1(immd_L), .out(Rt_ID), .sel(SSET));
  Forward_main main_5 (
    .Reg_Wr_EX(Reg_write_EX), .Reg_Wr_MEM(reg_write_mem), .Reg_Wr_WB(reg_write_WB), .Rs(Rs_ID), .Rt(Rt_ID),
    .Forwad_A(Forward_A), .Rd_EX(RD_EX), .Rd_MEM(rd_mem), .Rd_WB(rd_WB), .Stall(Stall),
    .MEM_Read_EX(MEM_Read_EX), .Forwad_B(Forwad_B));
  Multiplexer #(.width(32), .enable("false")) multiplexer_2 (
    .in0(bit_extender_2_out), .in1(bit_extender_3_out), .out(multiplexer_2_out), .sel(EXT_OP));
  // Probe on multiplexer_3_out
  regfile_new_main main_6 (
    .Ra(Rs_ID), .Rb(Rt_ID), .Rw(rd_WB), .Reg_write(reg_write_WB), .Bus_W(multiplexer_3_out), .Bus_A(BusA_ID),
    .Bus_B(main_6_bus_b), .Clk(clock_1_out), .R1(out_2), .R2(out_3), .R3(out_4), .R4(out_5), .R0(out_1),
    .R5(out_6), .R6(out_7), .R7(out_8), .R8(out_9), .R9(out_10), .R10(out_11), .R11(out_12), .R12(out_13),
    .R13(out_14), .R14(out_15), .R15(out_16), .R16(out_17), .R17(out_18), .R18(out_19), .R19(out_20),
    .R20(out_21), .R21(out_22), .R22(out_23), .R23(out_24), .R24(out_25), .R25(out_26), .R26(out_27),
    .R27(out_28), .R28(out_29), .R29(out_30), .R30(out_31), .R31(out_32));
  Multiplexer #(.select(2), .width(32), .enable("false")) multiplexer_3 (
    .in0({BUSB_EX[15:0], imm16_16bit_EX}), .in1({imm16_32_EX, imm16_16bit_EX}), .in2(multiplexer_5_out),
    .in3(bit_extender_4_out), .out(multiplexer_3_out), .sel(rd_src_WB));
  assign bit_extender_4_out = {{12{PC_plus_1_WB[19]}}, PC_plus_1_WB};  // Bit_Extender bit_extender_4
  block1 block1_1 (.op_code(opcode), .ALU_OP(ALU_OP), .func(func_4bit));
  // Probe on PC_plus_1_WB
  id_ex_main main_7 (
    .in_1(Stall), .in_2(clock_1_out), .imm16(multiplexer_2_out), .immL_immU(immdL_immdU), .BusA(BusA_ID),
    .BusB(main_6_bus_b), .Rs(Rs_ID), .Rt(Rt_ID), .PC_plus_1(PC_Plus_1_ID), .MEM_Read(MEM_Read),
    .MEM_Write(MEM_Write), .WB(WB), .Reg_Write(Reg_write), .Reg_Des(Rd_SRC), .RD(immd_L),
    .out_18({imm16_32_EX, imm16_16bit_EX}), .out_19(immdL_immdU_EX), .out_20(main_7_out_20),
    .out_21(BUSB_EX), .out_22(Rs_EX), .out_23(Rt_EX), .out_24(PC_Plus_1_EX), .out_25(MEM_Read_EX),
    .out_26(MEM_Write_EX), .out_27(WB_EX), .out_28(Reg_write_EX), .out_29(Rd_SRC_EX), .out_30(RD_EX),
    .ALU_OP(ALU_OP), .out_31(ALU_OP_EX), .ALU_SRC(ALU_SRC), .out_32(ALU_SRC_EX));
  Multiplexer #(.select(2), .width(32), .enable("false")) multiplexer_4 (
    .in0(BUSB_EX), .in1({imm16_32_EX, imm16_16bit_EX}), .in2(immdL_immdU_EX), .out(multiplexer_4_out),
    .sel(ALU_SRC_EX));  // open: in3
  ALU alu_1 (
    .ALU_Result(alu_1_alu_result), .less_flag_unsign(less_falg), .less_flag(less_Unsign_falg),
    .Zero_flag(Zero_flag), .A(main_7_out_20), .B(multiplexer_4_out), .ALU_Opration(ALU_OP_EX));  // open: Overflow
  ex_mem_main main_8 (
    .in_1(clock_1_out), .in_2(Stall), .WB(WB_EX), .MEM_Read(MEM_Read_EX), .MEM_Write(MEM_Write_EX),
    .Reg_write(Reg_write_EX), .Rd_src(Rd_SRC_EX), .PC_plus_1(PC_Plus_1_EX), .Rd(RD_EX), .Bus_B(BUSB_EX),
    .Alu_res(alu_1_alu_result), .out_12(WB_mem), .out_13(MEM_Read_mem), .out_14(MEM_Write_mem),
    .out_15(reg_write_mem), .out_16(rd_src_mem), .out_17(pc_plus_1_mem), .out_18(rd_mem), .out_19(Bus_B_mem),
    .out_20(Alu_res_mem));
  Data_Mem_main main_9 (
    .Mem_Write(MEM_Write_mem), .Mem_Read(MEM_Read_mem), .Clk(clock_1_out), .Data_In(Bus_B_mem),
    .Data_Out(main_9_data_out), .Alu_Result(Alu_res_mem));
  mem_wb_main main_10 (
    .WB(WB_mem), .reg_write(reg_write_mem), .rd_src(rd_src_mem), .PC_Plus_1(pc_plus_1_mem), .rd(rd_mem),
    .stall(Stall), .clk(clock_1_out), .out_11(WB_WB), .out_12(reg_write_WB), .out_13(rd_src_WB),
    .out_14(PC_plus_1_WB), .out_15(rd_WB), .alu_res(Alu_res_mem), .out_16(main_10_out_16),
    .Data_out(main_9_data_out), .out_10(main_10_out_10));
  Multiplexer #(.width(32), .enable("false")) multiplexer_5 (
    .in0(main_10_out_16), .in1(main_10_out_10), .out(multiplexer_5_out), .sel(WB_WB));

  // Other names for the same wires on the sheet: RD_ID[4:0] = immd_L; imm16[8:5] = func_4bit;
  //   immd_U[10:0] = {imm16[15:9], func_4bit}; imm16_32_EX[15:0] = imm16_16bit_EX; R0[31:0] = out_1; R1[31:0] = out_2;
  //   R2[31:0] = out_3; R3[31:0] = out_4; R4[31:0] = out_5; R5[31:0] = out_6; R6[31:0] = out_7; R7[31:0] = out_8;
  //   R8[31:0] = out_9; R9[31:0] = out_10; R10[31:0] = out_11; R11[31:0] = out_12; R12[31:0] = out_13;
  //   R13[31:0] = out_14; R14[31:0] = out_15; R15[31:0] = out_16; R16[31:0] = out_17; R17[31:0] = out_18;
  //   R18[31:0] = out_19; R19[31:0] = out_20; R20[31:0] = out_21; R21[31:0] = out_22; R22[31:0] = out_23;
  //   R23[31:0] = out_24; R24[31:0] = out_25; R25[31:0] = out_26; R26[31:0] = out_27; R27[31:0] = out_28;
  //   R28[31:0] = out_29; R29[31:0] = out_30; R30[31:0] = out_31; R31[31:0] = out_32

  // Notes on the sheet:
  //   op_code
  //   function
  //   0-> SSET
  //   01-> SET
  //   10->ALU_Result
endmodule
